# Fritzing sketch I2C_Between_Arduino_and_ESP32 (saved by Fritzing 0.9.3b)

parts:
  M5STACK-M5CAMERA1 = M5STACK-M5CAMERA
  パーツ2 = Arduino Zero

nets:
  GND: M5STACK-M5CAMERA1.GND, パーツ2.GND
  VCC: M5STACK-M5CAMERA1.Vcc, パーツ2.5V
  N1: M5STACK-M5CAMERA1.SDA, パーツ2.A4/SDA
  N2: M5STACK-M5CAMERA1.SCL, パーツ2.A5/SCL

custom parts:
  M5STACK-M5CAMERA: PSRAM Camera Module with ESP32 WROVER (OV2640) M5Camera is a development board for image recognition. It features an ESP32(4M Flash + 520K RAM) chip and 2-Megapixel carmera(OV2640). M5Camera offers plenty of storage, with an extra 4 Mbyte PSRAM. It also supports image transmission via Wi-Fi and debuging through USB Type-C port. The hardware comes preloaded software, programmed by ESP-IDF. It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
  Arduino Zero: Arduino Zero is a simple and powerful 32-bit extension of the platform established by Arduino UNO. The Zero board aims to provide creative individuals with the potential to realize truly innovative ideas for smart IoT devices, wearable technology, high-tech automation, crazy robotics, and projects not yet imagined. The board is powered by Atmel’s SAMD21 MCU, which features a 32-bit ARM Cortex®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

// code stored in the sketch: LED.ino
#define BPS 9600
#define PIN_GPIO_2 2
#define PIN_GPIO_3 3
#define PIN_GPIO_4 4
#define PIN_GPIO_5 5
#define PIN_GPIO_6 6
#define PIN_GPIO_7 7
#define PIN_GPIO_8 8
#define PIN_GPIO_9 9
#define PIN_GPIO_10 10
#define PIN_GPIO_11 11
#define PIN_LED PIN_GPIO_2


void setup() {
   pinMode(PIN_LED, OUTPUT);
   Serial.begin(BPS);
}

void loop() {
  digitalWrite(PIN_LED, HIGH);
  delay(1000);
  digitalWrite(PIN_LED, LOW);
  delay(1000);
}
